# Fritzing sketch InfoNinja (saved by Fritzing 0.7.0b)

parts:
  Arduino1 = Arduino
  LCD1 = LCD screen
  R2 = Rotary Potentiometer (Small) [maximum_resistance=100kΩ]
  LED1 = LED - 5mm [color="Red (633nm)" package="5 mm [THT]"]
  LED2 = LED - 5mm [color="Green (555nm)" package="5 mm [THT]"]
  LED3 = LED - 5mm [color="Blue (430nm)" package="5 mm [THT]"]
  S1 = Round Pushbutton
  S2 = Round Pushbutton
  S3 = Round Pushbutton
  LED4 = LED - 5mm [color="Red (633nm)" package="5 mm [THT]"]
  LED5 = LED - 5mm [color="Green (555nm)" package="5 mm [THT]"]
  LED6 = LED - 5mm [color="White (8000K)" package="5 mm [THT]"]

nets:
  GND: Arduino1.GND, LCD1.VSS, LCD1.R/W, R2.leg1, S1.leg1, S2.leg1, S3.leg1, LED4.cathode, LED5.cathode, LED6.cathode
  N1: Arduino1.D8, LCD1.E
  N2: Arduino1.D7, LCD1.DB6
  N3: Arduino1.D6, LED2.cathode
  N4: Arduino1.D5, LED1.cathode
  N5: Arduino1.D4, LCD1.DB7
  N6: Arduino1.D3, LED3.cathode
  N7: Arduino1.D2, LCD1.RS
  +5V: Arduino1.+5V, LCD1.VDD, LCD1.LED+, R2.leg2, LED6.anode
  N8: Arduino1.A0, S2.leg0
  N9: Arduino1.A1, S1.leg0
  N10: Arduino1.A2, S3.leg0
  N11: Arduino1.A3, LED4.anode, LED5.anode
  N12: Arduino1.A4, LCD1.DB5
  N13: Arduino1.A5, LCD1.DB4
  N14: LCD1.V0, R2.wiper
